# Fritzing sketch remote-switch (saved by Fritzing 0.9.3b)
breadboards: 1

parts:
  Part1 = Arduino Yun
  S1 = Pushbutton [package="[THT]"]  # not connected
  R1 = Resistor [tolerance=±5% resistance=10k package=THT]

nets:
  N1: Part1.GND, Part1.D2/SDA, Part1.D2, R1.Pin_1

// code stored in the sketch: oddball_yun.ino

